// Logisim project control-logic.circ as structural Verilog: 1 circuit, main circuit control_logic
module control_logic (
  input  [31:0] inst,
  input  BrEq,
  input  BrLt,
  output PCSel,
  output RegWEn,
  output [2:0] ImmSel,
  output BrUn,
  output ASel,
  output BSel,
  output [3:0] ALUSel,
  output MemRW,
  output [1:0] WBSel,
  output CSRSel,
  output CSRWen
);

  wire and_7_out, and_8_out, and_9_out, and_18_out, and_19_out, and_20_out, and_21_out, and_22_out,
       and_23_out, and_24_out, and_25_out, and_26_out, and_28_out, and_30_out, and_32_out, BeqPC, BgePC,
       BgeuPC, BltPC, BltuPC, BnePC, comparator_1_eq, comparator_2_eq, comparator_3_eq, comparator_4_eq,
       comparator_5_eq, comparator_6_eq, comparator_7_eq, comparator_8_eq, comparator_9_eq, comparator_10_eq,
       comparator_11_eq, comparator_13_eq, comparator_14_eq, comparator_15_eq, comparator_16_eq,
       comparator_17_eq, comparator_18_eq, comparator_19_eq, comparator_20_eq, comparator_21_eq,
       comparator_22_eq, comparator_23_eq, comparator_24_eq, comparator_26_eq, comparator_27_eq,
       comparator_28_eq, comparator_29_eq, comparator_30_eq, comparator_31_eq, comparator_32_eq,
       comparator_33_eq, comparator_34_eq, comparator_35_eq, comparator_36_eq, comparator_37_eq,
       comparator_39_eq, comparator_40_eq, comparator_41_eq, comparator_42_eq, comparator_43_eq,
       comparator_44_eq, comparator_45_eq, comparator_46_eq, comparator_47_eq, comparator_49_eq,
       comparator_50_eq, comparator_51_eq, comparator_53_eq, comparator_59_eq, comparator_60_eq, is_add,
       is_addi, is_and, is_andi, is_auipc, is_beq, is_bge, is_bgeu, is_blt, is_bltu, is_bne, is_csrw,
       is_csrwi, is_i_type, is_i_type_all_other, is_i_type_csr, is_i_type_load, is_jal, is_jalr, is_lb,
       is_lh, is_lui, is_lw, is_mul, is_mulh, is_mulhu, is_or, is_ori, is_r_type, is_s_type_store, is_sb,
       is_sb_type, is_sh, is_sll, is_slli, is_slt, is_slti, is_sra, is_srai, is_srl, is_srli, is_sub, is_sw,
       is_xor, is_xori, not_1_out, not_2_out, not_3_out, or_1_out;
  wire [4:0] is_1, is_2;
  wire [5:0] bit_extender_2_out, is_1_ext, is_2_ext, multiplexer_1_out;

  assign is_1_ext = {{1{1'b0}}, is_1};  // Bit_Extender bit_extender_1
  assign bit_extender_2_out = {{1{1'b0}}, is_2};  // Bit_Extender bit_extender_2
  Adder #(.width(6)) adder_1 (.a(bit_extender_2_out), .b(6'b100000), .out(is_2_ext));  // open: cin, cout
  or or_1 (or_1_out, is_auipc, is_lui, is_jal, is_jalr, is_i_type_csr);
  Multiplexer #(.enable("false"), .width(6)) multiplexer_1 (
    .in0(is_1_ext), .in1(is_2_ext), .out(multiplexer_1_out), .sel(or_1_out));
  ROM #(.addrWidth(6), .dataWidth(16)) rom_1 (
    .addr(multiplexer_1_out), .data({RegWEn, ImmSel, BrUn, ASel, BSel, ALUSel, MemRW, WBSel, CSRSel, CSRWen}));
  Priority_Encoder #(.select(5)) priority_encoder_1 (
    .in0(is_add), .in1(is_mul), .in2(is_sub), .in3(is_sll), .in4(is_mulh), .in5(is_mulhu), .in6(is_slt),
    .in7(is_xor), .in8(is_srl), .in9(is_sra), .in10(is_or), .in11(is_and), .in12(is_lb), .in13(is_lh),
    .in14(is_lw), .in15(is_addi), .in16(is_slli), .in17(is_slti), .in18(is_xori), .in19(is_srli),
    .in20(is_srai), .in21(is_ori), .in22(is_andi), .in23(is_sb), .in24(is_sh), .in25(is_sw), .in26(is_beq),
    .in27(is_bne), .in28(is_blt), .in29(is_bge), .in30(is_bltu), .in31(is_bgeu), .out(is_1));  // open: gs, en_out, en_in
  Priority_Encoder #(.select(5)) priority_encoder_2 (
    .in0(is_auipc), .in1(is_lui), .in2(is_jal), .in3(is_jalr), .in4(is_csrw), .in5(is_csrwi), .out(is_2));  // open: in6, in7, in8, in9, in10, in11, in12, in13, in14, in15, in16, in17, in18, in19, in20, in21, in22, in23, in24, in25, in26, in27, in28, in29, in30, in31, gs, en_out, en_in
  and and_1 (BeqPC, is_beq, BrEq);
  and and_2 (BnePC, is_bne, not_1_out);
  not not_1 (not_1_out, BrEq);
  and and_3 (BltPC, is_blt, BrLt);
  or or_2 (PCSel, BeqPC, BnePC, BltPC, BgePC, BltuPC, BgeuPC, is_jal, is_jalr);
  and and_4 (BgePC, is_bge, not_2_out);
  not not_2 (not_2_out, BrLt);
  and and_5 (BltuPC, is_bltu, BrLt);
  and and_6 (BgeuPC, is_bgeu, not_3_out);
  not not_3 (not_3_out, BrLt);
  Comparator #(.width(3)) comparator_1 (.a(inst[14:12]), .b(3'b001), .eq(comparator_1_eq));  // open: gt, lt
  Comparator #(.width(3)) comparator_2 (.a(inst[14:12]), .b(3'b101), .eq(comparator_2_eq));  // open: gt, lt
  Comparator #(.width(3)) comparator_3 (.a(inst[14:12]), .b(3'b000), .eq(comparator_3_eq));  // open: gt, lt
  Comparator #(.width(3)) comparator_4 (.a(inst[14:12]), .b(3'b010), .eq(comparator_4_eq));  // open: gt, lt
  Comparator #(.width(3)) comparator_5 (.a(inst[14:12]), .b(3'b100), .eq(comparator_5_eq));  // open: gt, lt
  Comparator #(.width(3)) comparator_6 (.a(inst[14:12]), .b(3'b101), .eq(comparator_6_eq));  // open: gt, lt
  Comparator #(.width(3)) comparator_7 (.a(inst[14:12]), .b(3'b110), .eq(comparator_7_eq));  // open: gt, lt
  Comparator #(.width(3)) comparator_8 (.a(inst[14:12]), .b(3'b111), .eq(comparator_8_eq));  // open: gt, lt
  and and_7 (and_7_out, is_i_type, comparator_1_eq);
  Comparator #(.width(7)) comparator_9 (.a(inst[31:25]), .b({7{1'b0}}), .eq(comparator_9_eq));  // open: gt, lt
  and and_8 (and_8_out, is_i_type, comparator_6_eq);
  Comparator #(.width(7)) comparator_10 (.a(inst[31:25]), .b({7{1'b0}}), .eq(comparator_10_eq));  // open: gt, lt
  and and_9 (and_9_out, is_i_type, comparator_2_eq);
  Comparator #(.width(7)) comparator_11 (.a(inst[31:25]), .b(7'b0100000), .eq(comparator_11_eq));  // open: gt, lt
  Comparator #(.width(7)) comparator_12 (.a(inst[6:0]), .b(7'b0010011), .eq(is_i_type));  // open: gt, lt
  and and_10 (is_addi, is_i_type, comparator_3_eq);
  and and_11 (is_slli, and_7_out, comparator_9_eq);
  and and_12 (is_slti, is_i_type, comparator_4_eq);
  and and_13 (is_xori, is_i_type, comparator_5_eq);
  and and_14 (is_srli, and_8_out, comparator_10_eq);
  and and_15 (is_srai, and_9_out, comparator_11_eq);
  and and_16 (is_ori, is_i_type, comparator_7_eq);
  and and_17 (is_andi, is_i_type, comparator_8_eq);
  Comparator #(.width(3)) comparator_13 (.a(inst[14:12]), .b(3'b000), .eq(comparator_13_eq));  // open: gt, lt
  Comparator #(.width(3)) comparator_14 (.a(inst[14:12]), .b(3'b000), .eq(comparator_14_eq));  // open: gt, lt
  Comparator #(.width(3)) comparator_15 (.a(inst[14:12]), .b(3'b000), .eq(comparator_15_eq));  // open: gt, lt
  Comparator #(.width(3)) comparator_16 (.a(inst[14:12]), .b(3'b001), .eq(comparator_16_eq));  // open: gt, lt
  Comparator #(.width(3)) comparator_17 (.a(inst[14:12]), .b(3'b001), .eq(comparator_17_eq));  // open: gt, lt
  Comparator #(.width(3)) comparator_18 (.a(inst[14:12]), .b(3'b011), .eq(comparator_18_eq));  // open: gt, lt
  Comparator #(.width(3)) comparator_19 (.a(inst[14:12]), .b(3'b010), .eq(comparator_19_eq));  // open: gt, lt
  Comparator #(.width(3)) comparator_20 (.a(inst[14:12]), .b(3'b100), .eq(comparator_20_eq));  // open: gt, lt
  Comparator #(.width(3)) comparator_21 (.a(inst[14:12]), .b(3'b101), .eq(comparator_21_eq));  // open: gt, lt
  Comparator #(.width(3)) comparator_22 (.a(inst[14:12]), .b(3'b101), .eq(comparator_22_eq));  // open: gt, lt
  Comparator #(.width(3)) comparator_23 (.a(inst[14:12]), .b(3'b110), .eq(comparator_23_eq));  // open: gt, lt
  Comparator #(.width(3)) comparator_24 (.a(inst[14:12]), .b(3'b111), .eq(comparator_24_eq));  // open: gt, lt
  Comparator #(.width(7)) comparator_25 (.a(inst[6:0]), .b(7'b0110011), .eq(is_r_type));  // open: gt, lt
  and and_18 (and_18_out, is_r_type, comparator_13_eq);
  Comparator #(.width(7)) comparator_26 (.a(inst[31:25]), .b({7{1'b0}}), .eq(comparator_26_eq));  // open: gt, lt
  and and_19 (and_19_out, is_r_type, comparator_14_eq);
  Comparator #(.width(7)) comparator_27 (.a(inst[31:25]), .b(7'b0000001), .eq(comparator_27_eq));  // open: gt, lt
  and and_20 (and_20_out, is_r_type, comparator_15_eq);
  Comparator #(.width(7)) comparator_28 (.a(inst[31:25]), .b(7'b0100000), .eq(comparator_28_eq));  // open: gt, lt
  and and_21 (and_21_out, is_r_type, comparator_16_eq);
  Comparator #(.width(7)) comparator_29 (.a(inst[31:25]), .b({7{1'b0}}), .eq(comparator_29_eq));  // open: gt, lt
  and and_22 (and_22_out, is_r_type, comparator_17_eq);
  Comparator #(.width(7)) comparator_30 (.a(inst[31:25]), .b(7'b0000001), .eq(comparator_30_eq));  // open: gt, lt
  and and_23 (and_23_out, is_r_type, comparator_18_eq);
  Comparator #(.width(7)) comparator_31 (.a(inst[31:25]), .b(7'b0000001), .eq(comparator_31_eq));  // open: gt, lt
  and and_24 (and_24_out, is_r_type, comparator_19_eq);
  Comparator #(.width(7)) comparator_32 (.a(inst[31:25]), .b({7{1'b0}}), .eq(comparator_32_eq));  // open: gt, lt
  and and_25 (and_25_out, is_r_type, comparator_20_eq);
  Comparator #(.width(7)) comparator_33 (.a(inst[31:25]), .b({7{1'b0}}), .eq(comparator_33_eq));  // open: gt, lt
  and and_26 (and_26_out, is_r_type, comparator_21_eq);
  and and_27 (is_srl, and_26_out, comparator_34_eq);
  Comparator #(.width(7)) comparator_34 (.a(inst[31:25]), .b({7{1'b0}}), .eq(comparator_34_eq));  // open: gt, lt
  and and_28 (and_28_out, is_r_type, comparator_22_eq);
  and and_29 (is_sra, and_28_out, comparator_35_eq);
  Comparator #(.width(7)) comparator_35 (.a(inst[31:25]), .b(7'b0100000), .eq(comparator_35_eq));  // open: gt, lt
  and and_30 (and_30_out, is_r_type, comparator_23_eq);
  and and_31 (is_or, and_30_out, comparator_36_eq);
  Comparator #(.width(7)) comparator_36 (.a(inst[31:25]), .b({7{1'b0}}), .eq(comparator_36_eq));  // open: gt, lt
  and and_32 (and_32_out, is_r_type, comparator_24_eq);
  and and_33 (is_and, and_32_out, comparator_37_eq);
  Comparator #(.width(7)) comparator_37 (.a(inst[31:25]), .b({7{1'b0}}), .eq(comparator_37_eq));  // open: gt, lt
  and and_34 (is_add, and_18_out, comparator_26_eq);
  and and_35 (is_mul, and_19_out, comparator_27_eq);
  and and_36 (is_sub, and_20_out, comparator_28_eq);
  and and_37 (is_sll, and_21_out, comparator_29_eq);
  and and_38 (is_mulh, and_22_out, comparator_30_eq);
  and and_39 (is_mulhu, and_23_out, comparator_31_eq);
  and and_40 (is_slt, and_24_out, comparator_32_eq);
  and and_41 (is_xor, and_25_out, comparator_33_eq);
  Comparator #(.width(7)) comparator_38 (.a(inst[6:0]), .b(7'b1100011), .eq(is_sb_type));  // open: gt, lt
  Comparator #(.width(3)) comparator_39 (.a(inst[14:12]), .b(3'b000), .eq(comparator_39_eq));  // open: gt, lt
  Comparator #(.width(3)) comparator_40 (.a(inst[14:12]), .b(3'b001), .eq(comparator_40_eq));  // open: gt, lt
  Comparator #(.width(3)) comparator_41 (.a(inst[14:12]), .b(3'b100), .eq(comparator_41_eq));  // open: gt, lt
  Comparator #(.width(3)) comparator_42 (.a(inst[14:12]), .b(3'b101), .eq(comparator_42_eq));  // open: gt, lt
  Comparator #(.width(3)) comparator_43 (.a(inst[14:12]), .b(3'b110), .eq(comparator_43_eq));  // open: gt, lt
  Comparator #(.width(3)) comparator_44 (.a(inst[14:12]), .b(3'b111), .eq(comparator_44_eq));  // open: gt, lt
  and and_42 (is_beq, is_sb_type, comparator_39_eq);
  and and_43 (is_bne, is_sb_type, comparator_40_eq);
  and and_44 (is_blt, is_sb_type, comparator_41_eq);
  and and_45 (is_bge, is_sb_type, comparator_42_eq);
  and and_46 (is_bltu, is_sb_type, comparator_43_eq);
  and and_47 (is_bgeu, is_sb_type, comparator_44_eq);
  Comparator #(.width(3)) comparator_45 (.a(inst[14:12]), .b(3'b000), .eq(comparator_45_eq));  // open: gt, lt
  Comparator #(.width(3)) comparator_46 (.a(inst[14:12]), .b(3'b001), .eq(comparator_46_eq));  // open: gt, lt
  Comparator #(.width(3)) comparator_47 (.a(inst[14:12]), .b(3'b010), .eq(comparator_47_eq));  // open: gt, lt
  Comparator #(.width(7)) comparator_48 (.a(inst[6:0]), .b(7'b0100011), .eq(is_s_type_store));  // open: gt, lt
  Comparator #(.width(3)) comparator_49 (.a(inst[14:12]), .b(3'b000), .eq(comparator_49_eq));  // open: gt, lt
  Comparator #(.width(3)) comparator_50 (.a(inst[14:12]), .b(3'b001), .eq(comparator_50_eq));  // open: gt, lt
  Comparator #(.width(3)) comparator_51 (.a(inst[14:12]), .b(3'b010), .eq(comparator_51_eq));  // open: gt, lt
  Comparator #(.width(7)) comparator_52 (.a(inst[6:0]), .b(7'b0000011), .eq(is_i_type_load));  // open: gt, lt
  and and_48 (is_lb, is_i_type_load, comparator_45_eq);
  and and_49 (is_lh, is_i_type_load, comparator_46_eq);
  and and_50 (is_lw, is_i_type_load, comparator_47_eq);
  and and_51 (is_sb, is_s_type_store, comparator_49_eq);
  and and_52 (is_sh, is_s_type_store, comparator_50_eq);
  and and_53 (is_sw, is_s_type_store, comparator_51_eq);
  Comparator #(.width(3)) comparator_53 (.a(inst[14:12]), .b(3'b000), .eq(comparator_53_eq));  // open: gt, lt
  Comparator #(.width(7)) comparator_54 (.a(inst[6:0]), .b(7'b0010111), .eq(is_auipc));  // open: gt, lt
  Comparator #(.width(7)) comparator_55 (.a(inst[6:0]), .b(7'b0110111), .eq(is_lui));  // open: gt, lt
  Comparator #(.width(7)) comparator_56 (.a(inst[6:0]), .b(7'b1101111), .eq(is_jal));  // open: gt, lt
  Comparator #(.width(7)) comparator_57 (.a(inst[6:0]), .b(7'b1100111), .eq(is_i_type_all_other));  // open: gt, lt
  and and_54 (is_jalr, is_i_type_all_other, comparator_53_eq);
  Comparator #(.width(7)) comparator_58 (.a(inst[6:0]), .b(7'b1110011), .eq(is_i_type_csr));  // open: gt, lt
  Comparator #(.width(3)) comparator_59 (.a(inst[14:12]), .b(3'b001), .eq(comparator_59_eq));  // open: gt, lt
  Comparator #(.width(3)) comparator_60 (.a(inst[14:12]), .b(3'b101), .eq(comparator_60_eq));  // open: gt, lt
  and and_55 (is_csrw, is_i_type_csr, comparator_59_eq);
  and and_56 (is_csrwi, is_i_type_csr, comparator_60_eq);

  // Other names for the same wires on the sheet: opcode[6:0] = inst[6:0]; func3[2:0] = inst[14:12];
  //   func7[6:0] = inst[31:25]

  // Notes on the sheet:
  //   INPUTS to your circuit
  //   contents of rom_1 (hex, n*v repeats v):
  //   8004 8104 8184 8024 8124 8164 8044 8084 80a4 81a4 80c4 80e4 9200 9200 9200 9204 9224 9244 9284 92a4
  //   93a4 92c4 92e4 2210 2210 2210 4*3600 3e00 3e00 c604 c22c d608 e204 7003 7003
  //   ROM FOR CONTROL LOGIC
  //   DON'T CHANGE THE LOCATIONS OF THE INPUTS AND OUTPUTS!
  //   OUTPUT from your circuit
  //   CLOSE
  //   WIRE
  //   TO
  //   USE
  //   ROM
  //   PCSel
  //   is_u_type
  //   is_uj_type
endmodule
