// Logisim project cpu.circ as structural Verilog: 1 circuit, main circuit cpu
module cpu (
  input  clk,
  input  [31:0] INSTRUCTION,
  input  [31:0] MEM_READ_DATA,
  output [31:0] MEM_WRITE_ADDRESS,
  output [31:0] PROGRAM_COUNTER,
  output [31:0] ra,
  output [31:0] sp,
  output [31:0] t0,
  output [31:0] t1,
  output [31:0] t2,
  output [31:0] s0,
  output [31:0] s1,
  output [31:0] a0,
  output [31:0] tohost,
  output [3:0] MEM_WRITE_ENABLE,
  output [31:0] MEM_WRITE_DATA
);

  wire ASel, BrEq, BrLt, BrUn, BSel, comparator_2_eq, comparator_3_eq, comparator_4_eq, comparator_5_eq,
       comparator_6_eq, comparator_7_eq, comparator_8_eq, comparator_9_eq, comparator_10_eq,
       comparator_11_eq, comparator_12_eq, comparator_13_eq, comparator_14_eq, comparator_15_eq, CSRSel,
       CSRWen, is_s_type_store, is_sb1, is_sb2, is_sb3, is_sb4, is_sh1, is_sh2, is_sw, MemRW, PCSel, RegWEn;
  wire [1:0] WBSel;
  wire [2:0] control_logic_1_immsel, func3;
  wire [3:0] ALUSel;
  wire [4:0] bit_extender_3_out, bit_extender_4_out, shifter_4_out, shifter_6_out;
  wire [7:0] load_lb;
  wire [11:0] CSR_address;
  wire [15:0] load_lh;
  wire [19:0] INSTRUCTION_2;
  wire [31:0] CSR_din, imm, INSTRUCTION_OUTPUT, load_lb_ext, load_lh_ext, load_lw, multiplexer_1_out,
       multiplexer_3_out, multiplexer_4_out, pc4, pc4_2, PROGRAM_COUNTER_2, rd_output_load, Read_Data_1,
       Read_Data_2, sb_store, sh_store, shifter_1_out, shifter_2_out, shifter_3_out, shifter_5_out,
       WBSelOutput;

  Adder #(.width(32)) adder_1 (.a(PROGRAM_COUNTER), .b(32'h4), .out(pc4));  // open: cin, cout
  Register #(.width(32)) PC (.D(multiplexer_1_out), .clk(clk), .Q(PROGRAM_COUNTER));  // open: en, clr
  Multiplexer #(.enable("false"), .width(32)) multiplexer_1 (
    .in0(pc4), .in1(MEM_WRITE_ADDRESS), .out(multiplexer_1_out), .sel(PCSel));
  control_logic control_logic_1 (
    .CSRWen(CSRWen), .PCSel(PCSel), .RegWEn(RegWEn), .ImmSel(control_logic_1_immsel), .BrUn(BrUn),
    .ASel(ASel), .BSel(BSel), .ALUSel(ALUSel), .MemRW(MemRW), .WBSel(WBSel), .CSRSel(CSRSel),
    .inst({CSR_address, INSTRUCTION_2[19:15], func3, INSTRUCTION_2[11:0]}), .BrEq(BrEq), .BrLt(BrLt));
  imm_gen imm_gen_1 (
    .inst({CSR_address, INSTRUCTION_2[19:15], func3, INSTRUCTION_2[11:0]}), .ImmSel(control_logic_1_immsel),
    .imm(imm));
  Register #(.width(32)) register_1 (.D(PROGRAM_COUNTER), .clk(clk), .Q(PROGRAM_COUNTER_2));  // open: en, clr
  regfile regfile_1 (
    .rs1(INSTRUCTION_2[19:15]), .rs2(CSR_address[4:0]), .rd(INSTRUCTION_2[11:7]), .Write_Data(WBSelOutput),
    .RegWEn(RegWEn), .clk(clk), .ra(ra), .sp(sp), .t0(t0), .t1(t1), .t2(t2), .s0(s0), .s1(s1), .a0(a0),
    .Read_Data_1(Read_Data_1), .Read_Data_2(Read_Data_2));
  branch_comp branch_comp_1 (.rs1(Read_Data_1), .rs2(Read_Data_2), .BrUn(BrUn), .BrEq(BrEq), .BrLt(BrLt));
  Register #(.width(32)) register_2 (
    .D(INSTRUCTION_OUTPUT), .clk(clk), .Q({CSR_address, INSTRUCTION_2[19:15], func3, INSTRUCTION_2[11:0]}));  // open: en, clr
  Multiplexer #(.enable("false"), .width(32)) multiplexer_2 (
    .in0(INSTRUCTION), .in1(32'h13), .out(INSTRUCTION_OUTPUT), .sel(PCSel));
  Register #(.width(32)) register_3 (.D(pc4), .clk(clk), .Q(pc4_2));  // open: en, clr
  Multiplexer #(.enable("false"), .width(32)) multiplexer_3 (
    .in0(Read_Data_1), .in1(PROGRAM_COUNTER_2), .out(multiplexer_3_out), .sel(ASel));
  Multiplexer #(.enable("false"), .width(32)) multiplexer_4 (
    .in0(Read_Data_2), .in1(imm), .out(multiplexer_4_out), .sel(BSel));
  alu alu_1 (.Result(MEM_WRITE_ADDRESS), .A(multiplexer_3_out), .B(multiplexer_4_out), .ALUSel(ALUSel));
  // csr csr_1: pin names not known; wires that end beside it: CSR_address, CSR_din, CSRWen, clk, tohost
  Multiplexer #(.enable("false"), .width(32)) multiplexer_5 (.in0(Read_Data_1), .in1(imm), .out(CSR_din), .sel(CSRSel));
  Multiplexer #(.enable("false"), .select(2), .width(8)) multiplexer_6 (
    .in0(MEM_READ_DATA[7:0]), .in1(MEM_READ_DATA[15:8]), .in2(MEM_READ_DATA[23:16]),
    .in3(MEM_READ_DATA[31:24]), .out(load_lb), .sel(MEM_WRITE_ADDRESS[1:0]));
  Multiplexer #(.enable("false"), .select(2), .width(16)) multiplexer_7 (
    .in0(MEM_READ_DATA[15:0]), .in2(MEM_READ_DATA[31:16]), .out(load_lh), .sel(MEM_WRITE_ADDRESS[1:0]));  // open: in1, in3
  Multiplexer #(.enable("false"), .select(2), .width(32)) multiplexer_8 (
    .in0(MEM_READ_DATA), .out(load_lw), .sel(MEM_WRITE_ADDRESS[1:0]));  // open: in1, in2, in3
  assign load_lb_ext = {{24{load_lb[7]}}, load_lb};  // Bit_Extender bit_extender_1
  assign load_lh_ext = {{16{load_lh[15]}}, load_lh};  // Bit_Extender bit_extender_2
  Multiplexer #(.enable("false"), .select(3), .width(32)) multiplexer_9 (
    .in0(load_lb_ext), .in1(load_lh_ext), .in2(load_lw), .out(rd_output_load), .sel(func3));  // open: in3, in4, in5, in6, in7
  Comparator #(.width(7)) comparator_1 (.a(INSTRUCTION_2[6:0]), .b(7'b0100011), .eq(is_s_type_store));  // open: gt, lt
  Comparator #(.width(2)) comparator_2 (.a(MEM_WRITE_ADDRESS[1:0]), .b(2'b00), .eq(comparator_2_eq));  // open: gt, lt
  Comparator #(.width(3)) comparator_3 (.a(func3), .b(3'b000), .eq(comparator_3_eq));  // open: gt, lt
  Comparator #(.width(2)) comparator_4 (.a(MEM_WRITE_ADDRESS[1:0]), .b(2'b01), .eq(comparator_4_eq));  // open: gt, lt
  Comparator #(.width(3)) comparator_5 (.a(func3), .b(3'b000), .eq(comparator_5_eq));  // open: gt, lt
  Comparator #(.width(2)) comparator_6 (.a(MEM_WRITE_ADDRESS[1:0]), .b(2'b10), .eq(comparator_6_eq));  // open: gt, lt
  Comparator #(.width(3)) comparator_7 (.a(func3), .b(3'b000), .eq(comparator_7_eq));  // open: gt, lt
  Shifter #(.width(32)) shifter_1 (.in(Read_Data_2), .\dist (5'b11000), .out(shifter_1_out));
  assign bit_extender_3_out = {{3{MEM_WRITE_ADDRESS[1]}}, MEM_WRITE_ADDRESS[1:0]};  // Bit_Extender bit_extender_3
  Shifter #(.width(32)) shifter_2 (.in(Read_Data_2), .\dist (5'b10000), .out(shifter_2_out));
  assign bit_extender_4_out = {{3{MEM_WRITE_ADDRESS[1]}}, MEM_WRITE_ADDRESS[1:0]};  // Bit_Extender bit_extender_4
  and and_1 (is_sb1, is_s_type_store, comparator_2_eq, comparator_3_eq);
  and and_2 (is_sb2, is_s_type_store, comparator_4_eq, comparator_5_eq);
  and and_3 (is_sb3, is_s_type_store, comparator_6_eq, comparator_7_eq);
  and and_4 (is_sb4, is_s_type_store, comparator_8_eq, comparator_9_eq);
  Comparator #(.width(2)) comparator_8 (.a(MEM_WRITE_ADDRESS[1:0]), .b(2'b11), .eq(comparator_8_eq));  // open: gt, lt
  Comparator #(.width(3)) comparator_9 (.a(func3), .b(3'b000), .eq(comparator_9_eq));  // open: gt, lt
  Shifter #(.shift("lr"), .width(32)) shifter_3 (.in(shifter_1_out), .\dist (5'b11000), .out(shifter_3_out));
  Shifter #(.width(5)) shifter_4 (.in(bit_extender_3_out), .\dist (3'b011), .out(shifter_4_out));
  Shifter #(.shift("lr"), .width(32)) shifter_5 (.in(shifter_2_out), .\dist (5'b10000), .out(shifter_5_out));
  Shifter #(.width(5)) shifter_6 (.in(bit_extender_4_out), .\dist (3'b011), .out(shifter_6_out));
  Shifter #(.width(32)) shifter_7 (.in(shifter_3_out), .\dist (shifter_4_out), .out(sb_store));
  Shifter #(.width(32)) shifter_8 (.in(shifter_5_out), .\dist (shifter_6_out), .out(sh_store));
  Comparator #(.width(2)) comparator_10 (.a(MEM_WRITE_ADDRESS[1:0]), .b(2'b00), .eq(comparator_10_eq));  // open: gt, lt
  Comparator #(.width(3)) comparator_11 (.a(func3), .b(3'b001), .eq(comparator_11_eq));  // open: gt, lt
  Comparator #(.width(2)) comparator_12 (.a(MEM_WRITE_ADDRESS[1:0]), .b(2'b10), .eq(comparator_12_eq));  // open: gt, lt
  Comparator #(.width(3)) comparator_13 (.a(func3), .b(3'b001), .eq(comparator_13_eq));  // open: gt, lt
  Comparator #(.width(2)) comparator_14 (.a(MEM_WRITE_ADDRESS[1:0]), .b(2'b00), .eq(comparator_14_eq));  // open: gt, lt
  Comparator #(.width(3)) comparator_15 (.a(func3), .b(3'b010), .eq(comparator_15_eq));  // open: gt, lt
  Multiplexer #(.enable("false"), .select(2), .width(32)) multiplexer_10 (
    .in0(rd_output_load), .in1(MEM_WRITE_ADDRESS), .in2(pc4_2), .in3(imm), .out(WBSelOutput), .sel(WBSel));
  and and_5 (is_sh1, is_s_type_store, comparator_10_eq, comparator_11_eq);
  and and_6 (is_sh2, is_s_type_store, comparator_12_eq, comparator_13_eq);
  and and_7 (is_sw, is_s_type_store, comparator_14_eq, comparator_15_eq);
  Multiplexer #(.enable("false"), .select(3), .width(32)) multiplexer_11 (
    .in0(sb_store), .in1(sh_store), .in2(Read_Data_2), .out(MEM_WRITE_DATA), .sel(func3));  // open: in3, in4, in5, in6, in7
  Priority_Encoder #(.select(4)) priority_encoder_1 (
    .in0(1'b1), .in1(is_sb1), .in2(is_sb2), .in3(is_sh1), .in4(is_sb3), .in8(is_sb4), .in12(is_sh2),
    .in15(is_sw), .out(MEM_WRITE_ENABLE));  // open: in5, in6, in7, in9, in10, in11, in13, in14, gs, en_out, en_in

  // Other names for the same wires on the sheet: alu_result[31:0] = MEM_WRITE_ADDRESS;
  //   bottom_bits_MWA[1:0] = MEM_WRITE_ADDRESS[1:0]; opcode[6:0] = INSTRUCTION_2[6:0]; rd[4:0] = INSTRUCTION_2[11:7];
  //   INSTRUCTION_2 (some bits) = {CSR_address, func3}; rs1[4:0] = INSTRUCTION_2[19:15]; rs2[4:0] = CSR_address[4:0];
  //   sw_store[31:0] = Read_Data_2

  // Notes on the sheet:
  //   Output to IMEM
  //   IMEM (do **NOT** move this)
  //   Inputs from IMEM
  //   It is OK to move the PC, RegFile, ALU, MEM, Branch Comp, Imm Gen, and Control Logic to wherever is most convenient for you when constructing your CPU, and to delete this text
  //   Inputs/Outputs for testing. Do **NOT** move these.
  //   CSR INSTRUCTIONS
  //   LOAD INSTRUCTIONS
  //   Outputs To DMEM
  //   DMEM (do **NOT** move this)
  //   Inputs From DMEM
  //   STORE INSTRUCTIONS
endmodule
