// Logisim project imm-gen.circ as structural Verilog: 1 circuit, main circuit imm_gen
module imm_gen (
  input  [31:0] inst,
  input  [2:0] ImmSel,
  output [31:0] imm
);

  wire [31:0] imm_csr, imm_i, imm_jalr, imm_sb, imm_store, imm_u, imm_u_shifted, imm_uj;

  assign imm_i = {{20{inst[31]}}, inst[31:20]};  // Bit_Extender bit_extender_1
  assign imm_sb = {{19{inst[31]}}, {inst[31], inst[7], inst[30:25], inst[11:8], 1'b0}};  // Bit_Extender bit_extender_2
  Shifter #(.width(32)) shifter_1 (.in(imm_u), .\dist (5'b01100), .out(imm_u_shifted));
  assign imm_store = {{20{inst[31]}}, {inst[31:25], inst[11:7]}};  // Bit_Extender bit_extender_3
  assign imm_u = {{12{inst[31]}}, inst[31:12]};  // Bit_Extender bit_extender_4
  assign imm_uj = {{11{inst[31]}}, {inst[31], inst[19:12], inst[20], inst[30:21], 1'b0}};  // Bit_Extender bit_extender_5
  assign imm_jalr = {{20{inst[31]}}, inst[31:20]};  // Bit_Extender bit_extender_6
  assign imm_csr = {{27{1'b0}}, inst[19:15]};  // Bit_Extender bit_extender_7
  Multiplexer #(.enable("false"), .select(3), .width(32)) multiplexer_1 (
    .in1(imm_i), .in2(imm_store), .in3(imm_sb), .in4(imm_u_shifted), .in5(imm_uj), .in6(imm_jalr),
    .in7(imm_csr), .out(imm), .sel(ImmSel));  // open: in0

  // Other names for the same wires on the sheet: immediate_sb[12:1] = {inst[31], inst[7], inst[30:25], inst[11:8]};
  //   immediate_store[11:0] = {inst[31:25], inst[11:7]}; immediate_i[11:0] = inst[31:20];
  //   immediate_jalr[11:0] = inst[31:20]; immediate_u[19:0] = inst[31:12];
  //   immediate_uj[20:1] = {inst[31], inst[19:12], inst[20], inst[30:21]}; immediate_csr[4:0] = inst[19:15]

  // Notes on the sheet:
  //   INPUTS to your circuit
  //   DON'T CHANGE THE LOCATIONS OF THE INPUTS AND OUTPUTS!
  //   OUTPUT from your circuit
endmodule
